// Logisim project ALU 1st Trial Version.circ as structural Verilog: 1 circuit, main circuit main
module main (
  input  As,
  input  A1,
  input  A0,
  input  Bs,
  input  B1,
  input  B0,
  input  in_7,
  input  in_8
);

  wire adder_subtractor_p9, adder_subtractor_p10, adder_subtractor_p11, adder_subtractor_p12,
       adder_subtractor_p13, b2d_converter_1_a, b2d_converter_1_b, b2d_converter_1_c, b2d_converter_1_d,
       b2d_converter_1_e, b2d_converter_1_f, b2d_converter_1_g, multiplexer_1_out, multiplexer_2_out,
       multiplexer_3_out, multiplexer_4_out, multiplexer_5_out, multiplexer_6_out, multiplexer_7_out,
       multiplier_1_p1, multiplier_1_p8, multiplier_1_p9, multiplier_1_p10, multiplier_1_p11,
       multiplier_1_p12, remainder_div_by_0, remainder_out_11, remainder_r0, remainder_r1, remainder_zero;

  // adder_and_subtractor_3_bit_modified___2__main adder_subtractor: pin names not known; wires that end beside it: A0, A0, A1, B0, B1, As, Bs, in_7, adder_subtractor_p9, adder_subtractor_p10, adder_subtractor_p11, adder_subtractor_p12, adder_subtractor_p13
  // Multiplier multiplier_1: pin names not known; wires that end beside it: multiplier_1_p1, As, A1, A0, Bs, B1, B0, multiplier_1_p8, multiplier_1_p9, multiplier_1_p10, multiplier_1_p11, multiplier_1_p12
  Remainder_ALU_main remainder (
    .AS(As), .A1(A1), .A0(A0), .BS(Bs), .B1(B1), .B0(B0), .out_11(remainder_out_11), .R0(remainder_r0),
    .R1(remainder_r1), .div_by_0(remainder_div_by_0), .Zero(remainder_zero));
  Multiplexer #(.select(2)) multiplexer_1 (
    .in0(1'b0), .in1(1'b0), .in2(1'b0), .in3(remainder_div_by_0), .out(multiplexer_1_out), .sel({in_8, in_7}));  // open: en
  Multiplexer #(.select(2)) multiplexer_2 (
    .in0(adder_subtractor_p9), .in1(adder_subtractor_p9), .in2(multiplier_1_p1), .in3(remainder_zero),
    .out(multiplexer_2_out), .sel({in_8, in_7}));  // open: en
  Multiplexer #(.select(2)) multiplexer_3 (
    .in0(adder_subtractor_p13), .in1(adder_subtractor_p13), .in2(multiplier_1_p8), .in3(remainder_out_11),
    .out(multiplexer_3_out), .sel({in_8, in_7}));  // open: en
  Multiplexer #(.select(2)) multiplexer_4 (
    .in0(adder_subtractor_p10), .in1(adder_subtractor_p10), .in2(multiplier_1_p12), .in3(remainder_r0),
    .out(multiplexer_4_out), .sel({in_8, in_7}));  // open: en
  Multiplexer #(.select(2)) multiplexer_5 (
    .in0(adder_subtractor_p11), .in1(adder_subtractor_p11), .in2(multiplier_1_p11), .in3(remainder_r1),
    .out(multiplexer_5_out), .sel({in_8, in_7}));  // open: en
  Multiplexer #(.select(2)) multiplexer_6 (
    .in0(adder_subtractor_p12), .in1(adder_subtractor_p12), .in2(multiplier_1_p10), .in3(1'b0),
    .out(multiplexer_6_out), .sel({in_8, in_7}));  // open: en
  Multiplexer #(.select(2)) multiplexer_7 (
    .in0(1'b0), .in1(1'b0), .in2(multiplier_1_p9), .in3(1'b0), .out(multiplexer_7_out), .sel({in_8, in_7}));  // open: en
  LED Div_By_Zero (.in(multiplexer_1_out));
  LED Zero_Flag (.in(multiplexer_2_out));
  LED Sign (.in(multiplexer_3_out));
  B2D_converter b2d_converter_1 (
    .P3(multiplexer_7_out), .P2(multiplexer_6_out), .P1(multiplexer_5_out), .P0(multiplexer_4_out),
    .a(b2d_converter_1_a), .b(b2d_converter_1_b), .c(b2d_converter_1_c), .d(b2d_converter_1_d),
    .e(b2d_converter_1_e), .f(b2d_converter_1_f), .g(b2d_converter_1_g));
  _7_Segment_Display u_7_segment_display_1 (.g(multiplexer_3_out));  // open: f, a, b, e, d, c, dp
  _7_Segment_Display u_7_segment_display_2 (
    .g(b2d_converter_1_g), .f(b2d_converter_1_f), .a(b2d_converter_1_a), .b(b2d_converter_1_b),
    .e(b2d_converter_1_e), .d(b2d_converter_1_d), .c(b2d_converter_1_c));  // open: dp
endmodule
