// Logisim project Remainder ALU.circ as structural Verilog: 2 circuits, main circuit main
module main (
  input  AS,
  input  A1,
  input  A0,
  input  BS,
  input  B1,
  input  B0,
  output R0,
  output R1,
  output div_by_0,
  output Zero,
  output out_11
);

  wire and_1_out, and_2_out, and_3_out, n7_segment_1_a, n7_segment_1_b, n7_segment_1_c_2, n7_segment_1_d_2,
       n7_segment_1_e, n7_segment_1_f, n7_segment_1_g, nand_1_out, nor_2_out, nor_3_out, not_1_out, not_2_out;

  and and_1 (and_1_out, A1, not_1_out);
  not not_1 (not_1_out, A0);
  and and_2 (and_2_out, B1, B0);
  and and_3 (and_3_out, A0, B1);
  nand nand_1 (nand_1_out, A1, B0);
  and and_4 (R1, and_1_out, and_2_out);
  nor nor_1 (div_by_0, B1, B0);
  and and_5 (R0, and_3_out, nand_1_out);
  nor nor_2 (nor_2_out, R0, div_by_0);
  not not_2 (not_2_out, nor_2_out);
  nor nor_3 (nor_3_out, Zero, div_by_0);
  _7_segment u_7_segment_1 (
    .D(R1), .C(R0), .a(n7_segment_1_a), .b(n7_segment_1_b), .c_2(n7_segment_1_c_2), .d_2(n7_segment_1_d_2),
    .e(n7_segment_1_e), .f(n7_segment_1_f), .g(n7_segment_1_g));
  nor nor_4 (Zero, not_2_out, R1);
  _7_Segment_Display u_7_segment_display_1 (.g(out_11));  // open: f, a, b, e, d, c, dp
  and and_6 (out_11, nor_3_out, AS);
  _7_Segment_Display u_7_segment_display_2 (
    .g(n7_segment_1_g), .f(n7_segment_1_f), .a(n7_segment_1_a), .b(n7_segment_1_b), .e(n7_segment_1_e),
    .d(n7_segment_1_d_2), .c(n7_segment_1_c_2));  // open: dp
endmodule

module _7_segment (
  input  D,
  input  C,
  output a,
  output b,
  output c_2,
  output d_2,
  output e,
  output f,
  output g
);

  wire not_1_out, not_2_out, not_3_out, not_5_out, not_6_out;

  not not_1 (not_1_out, C);
  not not_2 (not_2_out, D);
  not not_3 (not_3_out, C);
  not not_4 (e, C);
  not not_5 (not_5_out, D);
  not not_6 (not_6_out, C);
  or or_1 (a, not_1_out, D);
  or or_2 (c_2, not_2_out, C);
  or or_3 (d_2, not_3_out, D);
  and and_1 (f, not_5_out, not_6_out);

  assign b = 1'b1;
  assign g = D;
endmodule
